# Fritzing sketch iboost-reverse (saved by Fritzing 0.9.9b)
breadboards: 1

parts:
  R1 = Resistor [tolerance=±5% resistance=220 package="1206 [SMD]"]
  S1 = SWITCH-DPDT [package=es]
  U1 = BATTERY-2 [package=battery-aaa]

nets (from the schematic view):
  N1: R1.Pin_0, S1.5
  N2: R1.Pin_1, S1.2
  N3: S1.1, S1.6, U1.+2
  N4: S1.3, S1.4, U1.-2
